// Logisim project l0321_Ex.circ as structural Verilog: 1 circuit, main circuit main
module main (
  input  [7:0] in_1,
  input  in_2,
  input  in_3,
  input  [7:0] in_4,
  input  in_5,
  input  in_6,
  input  [7:0] in_7,
  input  in_8,
  input  in_9,
  input  [7:0] in_10,
  input  in_11,
  input  in_12,
  input  in_13,
  input  in_14,
  input  [7:0] in_15,
  input  in_16,
  input  in_17,
  input  [7:0] in_18,
  input  in_19,
  input  in_20,
  input  in_21,
  input  in_22,
  input  [7:0] in_23,
  input  [7:0] in_24,
  input  [7:0] in_25,
  input  [2:0] in_26,
  input  [2:0] in_27,
  input  [7:0] in_28,
  input  [7:0] in_29,
  input  [2:0] in_30,
  input  [2:0] in_31,
  output out_32,
  output out_33,
  output [7:0] out_34,
  output out_35,
  output out_36,
  output [7:0] out_37,
  output out_38,
  output out_39,
  output out_40,
  output out_41,
  output [7:0] out_42,
  output out_43,
  output out_44,
  output [7:0] out_45,
  output [7:0] out_46,
  output [7:0] out_47,
  output [7:0] out_48,
  output [7:0] out_49
);

  buf buffer_1 (out_32, in_2);
  buf buffer_2 (out_35, in_5);
  and AND (out_38, in_8, in_11);
  or OR (out_40, in_13, in_16);
  xor XOR (out_43, in_19, in_21);
  Shifter shifter_1 (.in(in_24), .\dist (in_26), .out(out_46));
  Shifter #(.shift("lr")) shifter_2 (.in(in_28), .\dist (in_30), .out(out_48));
  not not_1 (out_33, in_3);
  not not_2 (out_36, in_6);
  nor NOR (out_41, in_14, in_17);
  xnor XNOR (out_44, in_20, in_22);
  nand NAND (out_39, in_9, in_12);
  Shifter shifter_3 (.in(in_25), .\dist (in_27), .out(out_47));
  Shifter #(.shift("lr")) shifter_4 (.in(in_29), .\dist (in_31), .out(out_49));
  assign out_34 = in_1 & in_4;  // AND_Gate AND_2, 8 bits wide
  assign out_37 = in_7 | in_10;  // OR_Gate OR_2, 8 bits wide
  assign out_42 = in_15 ^ in_18;  // XOR_Gate XOR_2, 8 bits wide
  assign out_45 = ~in_23;  // NOT_Gate NOT_3, 8 bits wide

  // Notes on the sheet:
  //   Buffer
  //   Shifter의 input에서 밑의 데이터가 왜 3비트인가?
  //   8자리를 움직이면 00000000 이 되므로 무의미 -> 자동으로 옮길수 있는 최대비트 지정
  //   만약 9비트라면 8자리를 움직여도 유의미하므로 최대로 옮길수 있는 비트를 4bit로 자동지정
  //   Not Gate
  //   Shift // >> << // unsigned 밖에 안됨
  //   | : 하나라도 1이면 1
  //   ^ : 서로 다를경우 1, 같으면 0
  //   ~ : 1은 0으로, 0은 1로
  //   20155342 지현규
  //   & : 모두 1일경우에만 1, 하나라도 0이면 0
endmodule
