// Logisim project l0328_Ex.circ as structural Verilog: 9 circuits, main circuit main
module main (
  input  in_1,
  input  in_2,
  input  in_3,
  input  in_4,
  input  in_5,
  input  in_6,
  output out_7,
  output out_8,
  output out_9
);

  wire and_1_out, not_1_out, not_2_out, not_3_out, not_4_out, not_5_out, not_6_out, or_1_out, or_2_out;

  not not_1 (not_1_out, in_1);
  and and_1 (and_1_out, not_1_out, in_2);
  not not_2 (not_2_out, in_3);
  not not_3 (not_3_out, in_4);
  not not_4 (not_4_out, in_6);
  or or_1 (or_1_out, in_3, in_4);
  or or_2 (or_2_out, not_2_out, not_3_out);
  or or_3 (out_9, in_5, not_4_out);
  or or_4 (out_7, and_1_out, in_2);
  not not_5 (not_5_out, or_1_out);
  not not_6 (not_6_out, or_2_out);
  or or_5 (out_8, not_5_out, not_6_out);

  // Notes on the sheet:
  //   과제1 : B'+A
endmodule

module Ex1 (
  input  A,
  input  B,
  output out_3
);

  wire not_1_out;

  not not_1 (not_1_out, B);
  or or_1 (out_3, A, not_1_out);

  // Notes on the sheet:
  //   과제1 : B'+A
endmodule

module Ex2 (
  input  A,
  input  B,
  input  C,
  input  A_2,
  input  B_2,
  input  C_2,
  output out_7,
  output out_8
);

  wire and_1_out, and_2_out, and_3_out, and_4_out, and_5_out, and_6_out, not_1_out, not_2_out, not_3_out,
       not_4_out, not_5_out, not_6_out;

  not not_1 (not_1_out, A);
  not not_2 (not_2_out, B);
  not not_3 (not_3_out, C);
  not not_4 (not_4_out, A_2);
  not not_5 (not_5_out, B_2);
  not not_6 (not_6_out, C_2);
  and and_1 (and_1_out, not_1_out, not_3_out);
  and and_2 (and_2_out, A, C);
  and and_3 (and_3_out, not_2_out, not_3_out);
  and and_4 (and_4_out, A_2, not_5_out);
  and and_5 (and_5_out, A_2, C_2);
  and and_6 (and_6_out, not_4_out, not_6_out);
  or or_1 (out_7, and_1_out, and_2_out, and_3_out);
  or or_2 (out_8, and_4_out, and_5_out, and_6_out);

  // Notes on the sheet:
  //   과제2 : B'C'+AC+A'C
  //   과제2 : AB'+AC+A'C'
endmodule

module Ex3 (
  input  A,
  input  B,
  input  C,
  output out_4
);

  wire and_1_out, and_2_out, not_1_out, not_2_out, not_3_out;

  not not_1 (not_1_out, A);
  not not_2 (not_2_out, B);
  not not_3 (not_3_out, C);
  and and_1 (and_1_out, not_1_out, not_2_out, not_3_out);
  and and_2 (and_2_out, A, B, C);
  or or_1 (out_4, and_2_out, and_1_out);

  // Notes on the sheet:
  //   과제3 : A'B'C+ABC
endmodule

module Ex4 (
  input  A,
  input  B,
  input  C,
  input  A_2,
  input  B_2,
  input  C_2,
  input  A_3,
  input  B_3,
  input  C_3,
  input  A_4,
  input  A_5,
  input  A_6,
  input  B_4,
  input  B_5,
  input  B_6,
  input  C_4,
  input  C_5,
  input  C_6,
  output out_19,
  output out_20,
  output out_21,
  output out_22,
  output out_23,
  output out_24
);

  wire and_1_out, and_2_out, and_3_out, and_4_out, and_5_out, and_6_out, and_7_out, and_8_out, and_9_out,
       and_10_out, and_11_out, and_12_out, not_1_out, not_2_out, not_3_out, not_4_out, not_5_out, not_6_out,
       not_7_out, not_8_out, not_9_out, not_10_out, not_11_out, not_12_out, not_13_out, not_14_out, or_1_out;

  not not_1 (not_1_out, A);
  and and_1 (and_1_out, not_1_out, not_4_out);
  not not_2 (not_2_out, A_4);
  not not_3 (not_3_out, B_4);
  not not_4 (not_4_out, B);
  and and_2 (and_2_out, B, not_1_out, not_5_out);
  and and_3 (and_3_out, not_2_out, not_3_out);
  and and_4 (and_4_out, not_2_out, C_6);
  not not_5 (not_5_out, C);
  or or_1 (or_1_out, A, not_5_out);
  not not_6 (not_6_out, or_1_out);
  or or_2 (out_24, and_3_out, and_4_out);
  or or_3 (out_19, and_1_out, and_2_out, not_6_out);
  not not_7 (not_7_out, A_2);
  not not_8 (not_8_out, B_2);
  and and_5 (and_5_out, A_2, C_2);
  not not_9 (not_9_out, B_5);
  and and_6 (and_6_out, not_7_out, not_8_out, C_2);
  and and_7 (and_7_out, A_5, C_5);
  and and_8 (and_8_out, not_9_out, C_5);
  or or_4 (out_20, and_5_out, and_6_out);
  or or_5 (out_22, and_7_out, and_8_out);
  and and_9 (and_9_out, B_3, C_3);
  not not_10 (not_10_out, A_3);
  not not_11 (not_11_out, A_6);
  not not_12 (not_12_out, C_4);
  not not_13 (not_13_out, B_3);
  and and_10 (and_10_out, not_10_out, not_13_out, not_14_out);
  and and_11 (and_11_out, not_11_out, not_12_out);
  not not_14 (not_14_out, C_3);
  and and_12 (and_12_out, B_3, not_14_out);
  or or_6 (out_23, B_6, and_11_out);
  or or_7 (out_21, and_9_out, and_10_out, and_12_out);

  // Notes on the sheet:
  //   A'B'+A'BC'+(A+C')'
  //   A'B'+A'C
  //   AC+A'B'C
  //   AC+B'C
  //   BC+A'B'C+BC'
  //   A'C'+B
endmodule

module Ex5 (
  input  A,
  input  B,
  input  C,
  output Y
);

  wire and_1_out, not_1_out, not_2_out;

  not not_1 (not_1_out, A);
  not not_2 (not_2_out, B);
  and and_1 (and_1_out, not_1_out, not_2_out);
  or or_1 (Y, and_1_out, C);

  // Notes on the sheet:
  //   A'B'+C
  //   A
  //   B
  //   0
  //   0
  //   0
  //   0
  //   0
  //   1
  //   0
  //   1
  //   1
  //   0
  //   1
  //   0
  //   1
  //   1
  //   1
  //   1
  //   C
  //   0
  //   1
  //   0
  //   1
  //   0
  //   1
  //   0
  //   1
  //   Y
  //   1
  //   1
  //   0
  //   1
  //   0
  //   1
  //   0
  //   1
endmodule

module Ex4_1 (
  input  A,
  input  B,
  input  C,
  input  A_2,
  input  B_2,
  input  C_2,
  output out_7,
  output out_8
);

  wire and_1_out, and_2_out, and_3_out, and_4_out, not_1_out, not_2_out, not_3_out, not_4_out, not_5_out,
       not_6_out, or_1_out;

  not not_1 (not_1_out, A);
  and and_1 (and_1_out, not_1_out, not_4_out);
  not not_2 (not_2_out, A_2);
  not not_3 (not_3_out, B_2);
  not not_4 (not_4_out, B);
  and and_2 (and_2_out, B, not_1_out, not_5_out);
  and and_3 (and_3_out, not_2_out, not_3_out);
  and and_4 (and_4_out, not_2_out, C_2);
  not not_5 (not_5_out, C);
  or or_1 (or_1_out, A, not_5_out);
  not not_6 (not_6_out, or_1_out);
  or or_2 (out_8, and_3_out, and_4_out);
  or or_3 (out_7, and_1_out, and_2_out, not_6_out);

  // Notes on the sheet:
  //   A'B'+A'BC'+(A+C')'
  //   A'B'+A'C
endmodule

module Ex4_2 (
  input  A,
  input  B,
  input  C,
  input  A_2,
  input  B_2,
  input  C_2,
  output out_7,
  output out_8
);

  wire and_1_out, and_2_out, and_3_out, and_4_out, not_1_out, not_2_out, not_3_out;

  not not_1 (not_1_out, A);
  not not_2 (not_2_out, B);
  and and_1 (and_1_out, A, C);
  not not_3 (not_3_out, B_2);
  and and_2 (and_2_out, not_1_out, not_2_out, C);
  and and_3 (and_3_out, A_2, C_2);
  and and_4 (and_4_out, not_3_out, C_2);
  or or_1 (out_7, and_1_out, and_2_out);
  or or_2 (out_8, and_3_out, and_4_out);

  // Notes on the sheet:
  //   AC+A'B'C
  //   AC+B'C
endmodule

module Ex4_3 (
  input  A,
  input  B,
  input  C,
  input  A_2,
  input  B_2,
  input  C_2,
  output out_7,
  output out_8
);

  wire and_1_out, and_2_out, and_3_out, and_4_out, not_1_out, not_2_out, not_3_out, not_4_out, not_5_out;

  and and_1 (and_1_out, B, C);
  not not_1 (not_1_out, A);
  not not_2 (not_2_out, A_2);
  not not_3 (not_3_out, C_2);
  not not_4 (not_4_out, B);
  and and_2 (and_2_out, not_1_out, not_4_out, not_5_out);
  and and_3 (and_3_out, not_2_out, not_3_out);
  not not_5 (not_5_out, C);
  and and_4 (and_4_out, B, not_5_out);
  or or_1 (out_8, B_2, and_3_out);
  or or_2 (out_7, and_1_out, and_2_out, and_4_out);

  // Notes on the sheet:
  //   BC+A'B'C+BC'
  //   A'C'+B
endmodule
