// Logisim project l0404_Ex.circ as structural Verilog: 9 circuits, main circuit main
module main (
  input  S0,
  input  S1,
  input  A,
  input  B,
  input  C,
  input  D,
  output out_7
);

  wire n2_1_mux_1_out_4, n2_1_mux_2_out_4;

  _2_1_Mux u_2_1_mux_1 (.D0(A), .D1(B), .S(S0), .out_4(n2_1_mux_1_out_4));
  _2_1_Mux u_2_1_mux_2 (.D0(C), .D1(D), .S(S0), .out_4(n2_1_mux_2_out_4));
  _2_1_Mux u_2_1_mux_3 (.D0(n2_1_mux_1_out_4), .D1(n2_1_mux_2_out_4), .S(S1), .out_4(out_7));
endmodule

module Q1 (
  input  A,
  input  B,
  input  C,
  output Y
);

  wire and_1_out, not_1_out, not_2_out, not_3_out;

  not not_1 (not_1_out, A);
  not not_2 (not_2_out, B);
  not not_3 (not_3_out, C);
  and and_1 (and_1_out, not_1_out, not_3_out);
  or or_1 (Y, and_1_out, not_2_out);

  // Notes on the sheet:
  //   A: pull=up
  //   문제1 : A'C'+B'
endmodule

module _2_1_Mux (
  input  S,
  input  D0,
  input  D1,
  output out_4
);

  wire and_1_out, and_2_out, not_1_out;

  not not_1 (not_1_out, S);
  and and_1 (and_1_out, not_1_out, D0);
  and and_2 (and_2_out, S, D1);
  or or_1 (out_4, and_1_out, and_2_out);

  // Notes on the sheet:
  //   과제4. S'D0+SD1 = Y
endmodule

module Q2 (
  input  A,
  input  B,
  input  C,
  output Y
);

  wire and_1_out, and_2_out, not_1_out, not_2_out;

  not not_1 (not_1_out, A);
  not not_2 (not_2_out, B);
  and and_1 (and_1_out, A, B);
  and and_2 (and_2_out, not_1_out, not_2_out);
  or or_1 (Y, and_1_out, and_2_out);

  // Notes on the sheet:
  //   과제2  :  A'B'+AB
endmodule

module Q3 (
  input  A,
  input  B,
  input  C,
  output Y
);

  wire not_1_out, not_2_out;

  not not_1 (not_1_out, A);
  not not_2 (not_2_out, C);
  or or_1 (Y, not_1_out, not_2_out);

  // Notes on the sheet:
  //   문제3 : A'+C' = Y
endmodule

module Q5 (
  input  A,
  input  B,
  input  C,
  input  D,
  output out_5
);

  wire and_1_out, and_2_out, and_3_out, not_1_out, not_2_out, not_3_out;

  not not_1 (not_1_out, A);
  not not_2 (not_2_out, C);
  not not_3 (not_3_out, D);
  and and_1 (and_1_out, not_1_out, B, not_2_out, not_3_out);
  and and_2 (and_2_out, A, B, C);
  and and_3 (and_3_out, C, D);
  or or_1 (out_5, and_1_out, and_2_out, and_3_out);

  // Notes on the sheet:
  //   문제5) : A'BC'D' + ABC + CD
endmodule

module Q6_2 (
  input  A,
  input  B,
  input  C,
  input  D,
  output Y
);

  wire not_1_out;

  not not_1 (not_1_out, A);
  or or_1 (Y, not_1_out, D);

  // Notes on the sheet:
  //   문제6-2)  A'+D
endmodule

module Q6_3 (
  input  A,
  input  B,
  input  C,
  input  D,
  output Y
);

  wire and_1_out, not_1_out, not_2_out, not_3_out;

  not not_1 (not_1_out, A);
  not not_2 (not_2_out, B);
  not not_3 (not_3_out, C);
  and and_1 (and_1_out, not_1_out, not_2_out);
  or or_1 (Y, and_1_out, not_3_out);

  // Notes on the sheet:
  //   문제6-3) A'B'+C'
endmodule

module Q6_1 (
  input  A,
  input  B,
  input  C,
  input  D,
  output out_5
);

  wire and_1_out, and_2_out, not_1_out, not_2_out;

  not not_1 (not_1_out, A);
  not not_2 (not_2_out, C);
  and and_1 (and_1_out, A, C);
  and and_2 (and_2_out, not_1_out, not_2_out);
  or or_1 (out_5, and_1_out, and_2_out);

  // Notes on the sheet:
  //   문제 6-1 ) A'C' + AC
endmodule
