// Logisim project l0411_Ex.circ as structural Verilog
module main (
  input  S0,
  input  _000,
  input  _100,
  input  S1,
  input  _010,
  input  _110,
  input  S2,
  input  _001,
  input  _101,
  input  _011,
  input  _111,
  output Y
);

  wire n2_1_mux_1_y, n2_1_mux_2_y, n2_1_mux_3_y, n2_1_mux_4_y, n2_1_mux_5_y, n2_1_mux_6_y;

  _2_1_MUX u_2_1_mux_1 (.D0(_000), .D1(_100), .S(S0), .Y(n2_1_mux_1_y));
  _2_1_MUX u_2_1_mux_2 (.D0(_010), .D1(_110), .S(S0), .Y(n2_1_mux_2_y));
  _2_1_MUX u_2_1_mux_3 (.D0(_001), .D1(_101), .S(S0), .Y(n2_1_mux_3_y));
  _2_1_MUX u_2_1_mux_4 (.D0(_011), .D1(_111), .S(S0), .Y(n2_1_mux_4_y));
  _2_1_MUX u_2_1_mux_5 (.D0(n2_1_mux_1_y), .D1(n2_1_mux_2_y), .S(S1), .Y(n2_1_mux_5_y));
  _2_1_MUX u_2_1_mux_6 (.D0(n2_1_mux_3_y), .D1(n2_1_mux_4_y), .S(S1), .Y(n2_1_mux_6_y));
  _2_1_MUX u_2_1_mux_7 (.D0(n2_1_mux_5_y), .D1(n2_1_mux_6_y), .S(S2), .Y(Y));
endmodule

module _2_1_MUX (
  input  S,
  input  D0,
  input  D1,
  output Y
);

  wire and_1_out, and_2_out, not_1_out;

  not not_1 (not_1_out, S);
  and and_1 (and_1_out, not_1_out, D0);
  and and_2 (and_2_out, S, D1);
  or or_1 (Y, and_1_out, and_2_out);
endmodule

module _8_1_MUX (
  input  S0,
  input  _000,
  input  _100,
  input  S1,
  input  _010,
  input  _110,
  input  S2,
  input  _001,
  input  _101,
  input  _011,
  input  _111,
  output Y
);

  wire n2_1_mux_1_y, n2_1_mux_2_y, n2_1_mux_3_y, n2_1_mux_4_y, n2_1_mux_5_y, n2_1_mux_6_y;

  _2_1_MUX u_2_1_mux_1 (.D0(_000), .D1(_100), .S(S0), .Y(n2_1_mux_1_y));
  _2_1_MUX u_2_1_mux_2 (.D0(_010), .D1(_110), .S(S0), .Y(n2_1_mux_2_y));
  _2_1_MUX u_2_1_mux_3 (.D0(_001), .D1(_101), .S(S0), .Y(n2_1_mux_3_y));
  _2_1_MUX u_2_1_mux_4 (.D0(_011), .D1(_111), .S(S0), .Y(n2_1_mux_4_y));
  _2_1_MUX u_2_1_mux_5 (.D0(n2_1_mux_1_y), .D1(n2_1_mux_2_y), .S(S1), .Y(n2_1_mux_5_y));
  _2_1_MUX u_2_1_mux_6 (.D0(n2_1_mux_3_y), .D1(n2_1_mux_4_y), .S(S1), .Y(n2_1_mux_6_y));
  _2_1_MUX u_2_1_mux_7 (.D0(n2_1_mux_5_y), .D1(n2_1_mux_6_y), .S(S2), .Y(Y));
endmodule

module _2_4_DECODER (
  input  A1,
  input  A0,
  output out_3
);

  wire not_1_out, not_2_out, Y0_out, Y1_out, Y2_out, Y3_out;

  not not_1 (not_1_out, A1);
  not not_2 (not_2_out, A0);
  and Y3 (Y3_out, not_1_out, not_2_out);
  and Y2 (Y2_out, not_1_out, A0);
  and Y1 (Y1_out, A1, not_2_out);
  and Y0 (Y0_out, A0, A1);
  or or_1 (out_3, Y3_out, Y2_out, Y1_out, Y0_out);

  // Notes on the sheet:
  //   00
  //   01
  //   10
  //   11
endmodule

module _2_4_DEC_XOR (
  input  A1,
  input  A0,
  output out_3,
  output XOR
);

  wire not_1_out, not_2_out, Y0_out, Y1_out, Y2_out, Y3_out;

  not not_1 (not_1_out, A1);
  not not_2 (not_2_out, A0);
  and Y3 (Y3_out, not_1_out, not_2_out);
  and Y2 (Y2_out, not_1_out, A0);
  and Y1 (Y1_out, A1, not_2_out);
  and Y0 (Y0_out, A0, A1);
  or or_1 (XOR, Y1_out, Y2_out);
  or or_2 (out_3, Y3_out, Y2_out, Y1_out, Y0_out);

  // Notes on the sheet:
  //   00
  //   01
  //   10
  //   11
endmodule

module _2_4_DECODERS (
  input  A1,
  input  A0,
  output AND,
  output OR,
  output NOR,
  output NAND
);

  wire not_1_out, not_2_out, Y0_out, Y1_out, Y2_out, Y3_out;

  not not_1 (not_1_out, A1);
  not not_2 (not_2_out, A0);
  and Y3 (Y3_out, not_1_out, not_2_out);
  and Y2 (Y2_out, not_1_out, A0);
  and Y1 (Y1_out, A1, not_2_out);
  and Y0 (Y0_out, A0, A1);
  buf or_1 (AND, Y0_out);  // OR_Gate
  or or_2 (OR, Y2_out, Y1_out, Y0_out);
  buf or_3 (NOR, Y3_out);  // OR_Gate
  or or_4 (NAND, Y2_out, Y1_out, Y0_out);

  // Notes on the sheet:
  //   00
  //   01
  //   10
  //   11
endmodule
