// Logisim project l0502_Ex.circ as structural Verilog: 5 circuits, main circuit main
module main (
  input  A,
  input  B,
  input  Cin,
  output S,
  output Cout
);

  wire and_1_out, and_2_out, xor_1_out;

  xor xor_1 (xor_1_out, A, B);
  xor xor_2 (S, xor_1_out, Cin);
  and and_1 (and_1_out, Cin, xor_1_out);
  and and_2 (and_2_out, A, B);
  or or_1 (Cout, and_1_out, and_2_out);

  // Notes on the sheet:
  //   실습1. 1 1bit abber
endmodule

module _4bit_Adder (
  input  A1,
  input  B1,
  input  A2,
  input  B2,
  input  A3,
  input  B3,
  input  A4,
  input  B4,
  output S1,
  output S2,
  output S3,
  output S4,
  output Cout
);

  wire n1bit_adder_1_cout, n1bit_adder_2_cout, n1bit_adder_3_cout;

  _1bit_Adder u_1bit_adder_1 (.A(A1), .B(B1), .Cin(1'b0), .S(S1), .Cout(n1bit_adder_1_cout));
  _1bit_Adder u_1bit_adder_2 (.A(A2), .B(B2), .Cin(n1bit_adder_1_cout), .S(S2), .Cout(n1bit_adder_2_cout));
  _1bit_Adder u_1bit_adder_3 (.A(A3), .B(B3), .Cin(n1bit_adder_2_cout), .S(S3), .Cout(n1bit_adder_3_cout));
  _1bit_Adder u_1bit_adder_4 (.A(A4), .B(B4), .Cin(n1bit_adder_3_cout), .S(S4), .Cout(Cout));

  // Notes on the sheet:
  //   실습2. 4bit Adder
endmodule

module _1bit_Adder (
  input  A,
  input  B,
  input  Cin,
  output S,
  output Cout
);

  wire and_1_out, and_2_out, xor_1_out;

  xor xor_1 (xor_1_out, A, B);
  xor xor_2 (S, xor_1_out, Cin);
  and and_1 (and_1_out, Cin, xor_1_out);
  and and_2 (and_2_out, A, B);
  or or_1 (Cout, and_1_out, and_2_out);

  // Notes on the sheet:
  //   실습1. 1 1bit abber
endmodule

module _4bit_Adder_Adv (
  input  [3:0] A,
  input  [3:0] B,
  output [3:0] S,
  output Overflow
);

  wire _1bit_Adder_2_cout, _1bit_Adder_3_cout, _1bit_Adder_cout;

  _1bit_Adder _1bit_Adder (.A(A[0]), .B(B[0]), .Cin(1'b0), .S(S[0]), .Cout(_1bit_Adder_cout));
  _1bit_Adder _1bit_Adder_2 (.A(A[1]), .B(B[1]), .Cin(_1bit_Adder_cout), .S(S[1]), .Cout(_1bit_Adder_2_cout));
  _1bit_Adder _1bit_Adder_3 (.A(A[2]), .B(B[2]), .Cin(_1bit_Adder_2_cout), .S(S[2]), .Cout(_1bit_Adder_3_cout));
  _1bit_Adder _1bit_Adder_4 (.A(A[3]), .B(B[3]), .Cin(_1bit_Adder_3_cout), .S(S[3]), .Cout(Overflow));

  // Notes on the sheet:
  //   4bit Adder (Advance)
endmodule

module TrafficLight (
  input  Ta,
  input  Tb,
  output LA1,
  output LA0,
  output LB1,
  output LB0
);

  wire and_1_out, and_2_out, clock_1_out, not_1_out, not_2_out, or_1_out, S0_prime_out, S0_q, S1_prime_out,
       xor_1_out;

  not not_1 (not_1_out, Ta);
  not not_2 (not_2_out, Tb);
  xor xor_1 (xor_1_out, LA1, S0_q);
  not S1_prime (S1_prime_out, LA1);
  not S0_prime (S0_prime_out, S0_q);
  and and_1 (and_1_out, not_1_out, S1_prime_out, S0_prime_out);
  and and_2 (and_2_out, S0_prime_out, LA1, not_2_out);
  or or_1 (or_1_out, and_1_out, and_2_out);
  Clock clock_1 (.out(clock_1_out));
  D_Flip_Flop S1 (.clk(clock_1_out), .D(xor_1_out), .Q(LA1));  // open: Qn, preset, en, reset
  D_Flip_Flop S0 (.clk(clock_1_out), .D(or_1_out), .Q(S0_q));  // open: Qn, preset, en, reset
  not not_3 (LB1, LA1);
  and and_3 (LA0, LB1, S0_q);
  and and_4 (LB0, LA1, S0_q);

  // Notes on the sheet:
  //   Traffic Light
endmodule
