// Logisim project l0509_Ex.circ as structural Verilog
module _4bit_ALU (
  input  [3:0] A,
  input  [3:0] B,
  input  [2:0] F,
  output [3:0] out_4,
  output Cout
);

  wire [3:0] adder_1_out, and_1_out, bit_extender_1_out, multiplexer_1_out, not_1_out, or_1_out;

  assign not_1_out = ~B;  // NOT_Gate not_1, 4 bits wide
  assign and_1_out = A & B;  // AND_Gate and_1, 4 bits wide
  assign or_1_out = A | B;  // OR_Gate or_1, 4 bits wide
  Multiplexer #(.width(4), .enable("false")) multiplexer_1 (
    .in0(B), .in1(not_1_out), .out(multiplexer_1_out), .sel(F[2]));
  Adder #(.width(4)) adder_1 (.a(A), .b(multiplexer_1_out), .out(adder_1_out), .cin(F[2]), .cout(Cout));
  assign bit_extender_1_out = {{3{1'b0}}, adder_1_out[3]};  // Bit_Extender bit_extender_1
  Multiplexer #(.select(2), .width(4), .enable("false")) multiplexer_2 (
    .in0(and_1_out), .in1(or_1_out), .in2(adder_1_out), .in3(bit_extender_1_out), .out(out_4), .sel(F[1:0]));

  // Notes on the sheet:
  //   4bit ALU - 20155342 지현규
endmodule

module _1bit_substracter (
  input  X,
  input  Y,
  input  Z,
  output D,
  output B
);

  wire and_1_out, and_2_out, not_1_out, xnor_1_out, xor_1_out;

  not not_1 (not_1_out, X);
  xor xor_1 (xor_1_out, X, Y);
  and and_1 (and_1_out, not_1_out, Y);
  xor xor_2 (D, xor_1_out, Z);
  xnor xnor_1 (xnor_1_out, X, Y);
  and and_2 (and_2_out, xnor_1_out, Z);
  or or_1 (B, and_1_out, and_2_out);

  // Notes on the sheet:
  //   1bit subtracter
endmodule

module _4bit_subtractor (
  input  [3:0] X,
  input  [3:0] Y,
  output [3:0] D,
  output B,
  output [3:0] out_5
);

  wire n1bit_substracter_1_b, n1bit_substracter_2_b, n1bit_substracter_3_b;

  Subtractor #(.width(4)) subtractor_1 (.a(X), .b(Y), .out(out_5));  // open: bin, bout
  _1bit_substracter u_1bit_substracter_1 (.X(X[0]), .Y(Y[0]), .Z(1'b0), .D(D[0]), .B(n1bit_substracter_1_b));
  _1bit_substracter u_1bit_substracter_2 (
    .X(X[1]), .Y(Y[1]), .Z(n1bit_substracter_1_b), .D(D[1]), .B(n1bit_substracter_2_b));
  _1bit_substracter u_1bit_substracter_3 (
    .X(X[2]), .Y(Y[2]), .Z(n1bit_substracter_2_b), .D(D[2]), .B(n1bit_substracter_3_b));
  _1bit_substracter u_1bit_substracter_4 (.X(X[3]), .Y(Y[3]), .Z(n1bit_substracter_3_b), .D(D[3]), .B(B));

  // Notes on the sheet:
  //   4bit subtractor
endmodule
