// Logisim project l0523_.circ as structural Verilog
module _1_Bit_Adder (
  input  A,
  input  B,
  output Cout,
  output S
);

  and and_1 (Cout, A, B);
  xor xor_1 (S, A, B);

  // Notes on the sheet:
  //   1bit Half Adder
endmodule

module _1_Bit_full_Adder (
  input  A,
  input  B,
  input  Cin,
  output S,
  output Cout
);

  wire and_1_out, and_2_out, xor_1_out;

  xor xor_1 (xor_1_out, A, B);
  xor xor_2 (S, xor_1_out, Cin);
  and and_1 (and_1_out, Cin, xor_1_out);
  and and_2 (and_2_out, B, A);
  or or_1 (Cout, and_1_out, and_2_out);

  // Notes on the sheet:
  //   1bit full Adder
endmodule

module _4bit_Sub (
  input  [3:0] A,
  input  [3:0] B,
  output [3:0] out_3
);

  wire n1_bit_full_adder_1_cout, n1_bit_full_adder_2_cout, n1_bit_full_adder_3_cout;
  wire [3:0] not_1_out;

  assign not_1_out = ~B;  // NOT_Gate not_1, 4 bits wide
  _1_Bit_full_Adder u_1_bit_full_adder_1 (
    .A(A[0]), .B(not_1_out[0]), .Cin(1'b1), .S(out_3[0]), .Cout(n1_bit_full_adder_1_cout));
  _1_Bit_full_Adder u_1_bit_full_adder_2 (
    .A(A[1]), .B(not_1_out[1]), .Cin(n1_bit_full_adder_1_cout), .S(out_3[1]), .Cout(n1_bit_full_adder_2_cout));
  _1_Bit_full_Adder u_1_bit_full_adder_3 (
    .A(A[2]), .B(not_1_out[2]), .Cin(n1_bit_full_adder_2_cout), .S(out_3[2]), .Cout(n1_bit_full_adder_3_cout));
  _1_Bit_full_Adder u_1_bit_full_adder_4 (
    .A(A[3]), .B(not_1_out[3]), .Cin(n1_bit_full_adder_3_cout), .S(out_3[3]));  // open: Cout

  // Notes on the sheet:
  //   4bit Subtractor
endmodule

module _2_1_MUX (
  input  S,
  input  D0,
  input  D1,
  output Y
);

  wire and_1_out, and_2_out, not_1_out;

  not not_1 (not_1_out, S);
  and and_1 (and_1_out, not_1_out, D0);
  and and_2 (and_2_out, S, D1);
  or or_1 (Y, and_1_out, and_2_out);

  // Notes on the sheet:
  //   2:1 MUX
endmodule

module _4_1_MUX (
  input  [1:0] S,
  input  D0,
  input  D1,
  input  D2,
  input  D3,
  output Y
);

  wire n2_1_mux_1_y, n2_1_mux_2_y;

  _2_1_MUX u_2_1_mux_1 (.S(S[0]), .D0(D0), .D1(D1), .Y(n2_1_mux_1_y));
  _2_1_MUX u_2_1_mux_2 (.S(S[0]), .D0(D2), .D1(D3), .Y(n2_1_mux_2_y));
  _2_1_MUX u_2_1_mux_3 (.S(S[1]), .D0(n2_1_mux_1_y), .D1(n2_1_mux_2_y), .Y(Y));

  // Notes on the sheet:
  //   4:1 MUX
endmodule

module Right_Shifter (
  input  [1:0] Shift,
  input  [3:0] Input,
  output [3:0] Output
);

  _4_1_MUX Y3 (.S(Shift), .D0(Input[3]), .D1(1'b0), .D2(1'b0), .D3(1'b0), .Y(Output[3]));
  _4_1_MUX Y2 (.S(Shift), .D0(Input[2]), .D1(Input[3]), .D2(1'b0), .D3(1'b0), .Y(Output[2]));
  _4_1_MUX Y1 (.S(Shift), .D0(Input[1]), .D1(Input[2]), .D2(Input[3]), .D3(1'b0), .Y(Output[1]));
  _4_1_MUX Y0 (.S(Shift), .D0(Input[0]), .D1(Input[1]), .D2(Input[2]), .D3(Input[3]), .Y(Output[0]));

  // Notes on the sheet:
  //   2. Right Shifter
endmodule

module Left_Shifter (
  input  [1:0] Shift,
  input  [3:0] Input,
  output [3:0] Output
);

  _4_1_MUX Y3 (.S(Shift), .D0(Input[3]), .D1(Input[2]), .D2(Input[1]), .D3(Input[0]), .Y(Output[3]));
  _4_1_MUX Y2 (.S(Shift), .D0(Input[2]), .D1(Input[1]), .D2(Input[0]), .D3(1'b0), .Y(Output[2]));
  _4_1_MUX Y1 (.S(Shift), .D0(Input[1]), .D1(Input[0]), .D2(1'b0), .D3(1'b0), .Y(Output[1]));
  _4_1_MUX Y0 (.S(Shift), .D0(Input[0]), .D1(1'b0), .D2(1'b0), .D3(1'b0), .Y(Output[0]));

  // Notes on the sheet:
  //   3. Left Shifter
endmodule

module Multi (
  input  [1:0] Shift,
  input  [3:0] X,
  output [3:0] _3_5X
);

  wire [3:0] Full_Adder_out_3, Left_output, Right_output;

  Left_Shifter Left (.Shift(Shift), .Input(X), .Output(Left_output));
  Right_Shifter Right (.Shift(Shift), .Input(X), .Output(Right_output));
  _4bit_Adder Full_Adder (.A(Left_output), .B(Right_output), .out_3(Full_Adder_out_3));
  _4bit_Adder Full_Adder_2 (.A(Full_Adder_out_3), .B(X), .out_3(_3_5X));

  // Notes on the sheet:
  //   1X
  //   4. MULTIPLE 3.5
  //   2X
  //   0.5X
  //   2.5X
endmodule

module _4bit_Adder (
  input  [3:0] A,
  input  [3:0] B,
  output [3:0] out_3
);

  wire n1_bit_full_adder_1_cout, n1_bit_full_adder_2_cout, n1_bit_full_adder_3_cout;

  _1_Bit_full_Adder u_1_bit_full_adder_1 (
    .A(A[0]), .B(B[0]), .Cin(1'b0), .S(out_3[0]), .Cout(n1_bit_full_adder_1_cout));
  _1_Bit_full_Adder u_1_bit_full_adder_2 (
    .A(A[1]), .B(B[1]), .Cin(n1_bit_full_adder_1_cout), .S(out_3[1]), .Cout(n1_bit_full_adder_2_cout));
  _1_Bit_full_Adder u_1_bit_full_adder_3 (
    .A(A[2]), .B(B[2]), .Cin(n1_bit_full_adder_2_cout), .S(out_3[2]), .Cout(n1_bit_full_adder_3_cout));
  _1_Bit_full_Adder u_1_bit_full_adder_4 (
    .A(A[3]), .B(B[3]), .Cin(n1_bit_full_adder_3_cout), .S(out_3[3]));  // open: Cout

  // Notes on the sheet:
  //   4bit Adder
endmodule
